// Digital circuit 4bit_MemoryModule.dig as structural Verilog
module _4bit_MemoryModule (
  input  [3:0] Data,
  input  [3:0] Write_Address,
  input  [3:0] Read_Input,
  input  Clock,
  output [3:0] Output
);

  wire [3:0] demultiplexer_1_out_0, demultiplexer_1_out_1, demultiplexer_1_out_2, demultiplexer_1_out_3,
       demultiplexer_1_out_4, demultiplexer_1_out_5, demultiplexer_1_out_6, demultiplexer_1_out_7,
       demultiplexer_1_out_8, demultiplexer_1_out_9, demultiplexer_1_out_10, demultiplexer_1_out_11,
       demultiplexer_1_out_12, demultiplexer_1_out_13, demultiplexer_1_out_14, demultiplexer_1_out_15,
       register_cpu_1_output, register_cpu_2_output, register_cpu_3_output, register_cpu_4_output,
       register_cpu_5_output, register_cpu_6_output, register_cpu_7_output, register_cpu_8_output,
       register_cpu_9_output, register_cpu_10_output, register_cpu_11_output, register_cpu_13_output,
       register_cpu_14_output, register_cpu_15_output, register_cpu_16_output;

  Demultiplexer #(.Selector_Bits(4), .Bits(4)) demultiplexer_1 (
    .sel(Write_Address), .in(Data), .out_0(demultiplexer_1_out_0), .out_1(demultiplexer_1_out_1),
    .out_2(demultiplexer_1_out_2), .out_3(demultiplexer_1_out_3), .out_4(demultiplexer_1_out_4),
    .out_5(demultiplexer_1_out_5), .out_6(demultiplexer_1_out_6), .out_7(demultiplexer_1_out_7),
    .out_8(demultiplexer_1_out_8), .out_9(demultiplexer_1_out_9), .out_10(demultiplexer_1_out_10),
    .out_11(demultiplexer_1_out_11), .out_12(demultiplexer_1_out_12), .out_13(demultiplexer_1_out_13),
    .out_14(demultiplexer_1_out_14), .out_15(demultiplexer_1_out_15));
  Register_CPU register_cpu_1 (.Input(demultiplexer_1_out_0), .Clock(Clock), .Output(register_cpu_1_output));
  Register_CPU register_cpu_2 (.Input(demultiplexer_1_out_1), .Clock(Clock), .Output(register_cpu_2_output));
  Register_CPU register_cpu_3 (.Input(demultiplexer_1_out_2), .Clock(Clock), .Output(register_cpu_3_output));
  Register_CPU register_cpu_4 (.Input(demultiplexer_1_out_3), .Clock(Clock), .Output(register_cpu_4_output));
  Register_CPU register_cpu_5 (.Input(demultiplexer_1_out_4), .Clock(Clock), .Output(register_cpu_5_output));
  Register_CPU register_cpu_6 (.Input(demultiplexer_1_out_5), .Clock(Clock), .Output(register_cpu_6_output));
  Register_CPU register_cpu_7 (.Input(demultiplexer_1_out_6), .Clock(Clock), .Output(register_cpu_7_output));
  Register_CPU register_cpu_8 (.Input(demultiplexer_1_out_7), .Clock(Clock), .Output(register_cpu_8_output));
  Register_CPU register_cpu_9 (.Input(demultiplexer_1_out_8), .Clock(Clock), .Output(register_cpu_9_output));
  Register_CPU register_cpu_10 (.Input(demultiplexer_1_out_9), .Clock(Clock), .Output(register_cpu_10_output));
  Register_CPU register_cpu_11 (.Input(demultiplexer_1_out_10), .Clock(Clock), .Output(register_cpu_11_output));
  Register_CPU register_cpu_12 (.Input(demultiplexer_1_out_11), .Clock(Clock), .Output(register_cpu_11_output));
  Register_CPU register_cpu_13 (.Input(demultiplexer_1_out_12), .Clock(Clock), .Output(register_cpu_13_output));
  Register_CPU register_cpu_14 (.Input(demultiplexer_1_out_13), .Clock(Clock), .Output(register_cpu_14_output));
  Register_CPU register_cpu_15 (.Input(demultiplexer_1_out_14), .Clock(Clock), .Output(register_cpu_15_output));
  Register_CPU register_cpu_16 (.Input(demultiplexer_1_out_15), .Clock(Clock), .Output(register_cpu_16_output));
  Multiplexer #(.Selector_Bits(4), .Bits(4)) multiplexer_1 (
    .sel(Read_Input), .in_0(register_cpu_1_output), .in_1(register_cpu_2_output),
    .in_2(register_cpu_3_output), .in_3(register_cpu_4_output), .in_4(register_cpu_5_output),
    .in_5(register_cpu_6_output), .in_6(register_cpu_7_output), .in_7(register_cpu_8_output),
    .in_8(register_cpu_9_output), .in_9(register_cpu_10_output), .in_10(register_cpu_11_output),
    .in_11(register_cpu_11_output), .in_12(register_cpu_13_output), .in_13(register_cpu_14_output),
    .in_14(register_cpu_15_output), .in_15(register_cpu_16_output), .out(Output));
endmodule
