// Digital circuit 4bit_RegisterFile.dig as structural Verilog
module _4bit_RegisterFile (
  input  [1:0] Read_register_1,
  input  [1:0] Read_register_2,
  input  [1:0] write_register,
  input  [3:0] Write_data,
  input  Clock,
  output [3:0] Read_data_1,
  output [3:0] Read_data_2
);

  wire [3:0] demultiplexer_1_out_0, demultiplexer_1_out_1, demultiplexer_1_out_2, demultiplexer_1_out_3,
       register_1_p3, register_2_p3, register_3_p3, register_4_p3;

  Demultiplexer #(.Selector_Bits(2), .Bits(4)) demultiplexer_1 (
    .sel(write_register), .in(Write_data), .out_0(demultiplexer_1_out_0), .out_1(demultiplexer_1_out_1),
    .out_2(demultiplexer_1_out_2), .out_3(demultiplexer_1_out_3));
  // Register register_1: pin names not known; wires that end beside it: Clock, demultiplexer_1_out_3, register_1_p3
  // Register register_2: pin names not known; wires that end beside it: Clock, demultiplexer_1_out_0, register_2_p3
  // Register register_3: pin names not known; wires that end beside it: Clock, demultiplexer_1_out_1, register_3_p3
  // Register register_4: pin names not known; wires that end beside it: Clock, demultiplexer_1_out_2, register_4_p3
  Multiplexer #(.Selector_Bits(2), .Bits(4)) multiplexer_1 (
    .sel(Read_register_1), .in_0(register_2_p3), .in_1(register_3_p3), .in_2(register_4_p3),
    .in_3(register_1_p3), .out(Read_data_1));
  Multiplexer #(.Selector_Bits(2), .Bits(4)) multiplexer_2 (
    .sel(Read_register_2), .in_0(register_2_p3), .in_1(register_3_p3), .in_2(register_4_p3),
    .in_3(register_1_p3), .out(Read_data_2));
endmodule
